// Logisim project CU.circ as structural Verilog
module CNTR (
  input  in_1,
  output Fetch,
  output Load,
  output Exe,
  output Sav
);

  wire not_1_out, not_2_out, not_3_out, not_4_out, t_ff_1_q, t_ff_1_qn, t_ff_2_q;

  T_Flip_Flop t_ff_1 (.T(1'b1), .clk(in_1), .Q(t_ff_1_q), .Qn(t_ff_1_qn));  // open: reset, preset
  not not_1 (not_1_out, t_ff_2_q);
  not not_2 (not_2_out, t_ff_1_q);
  and and_1 (Fetch, not_2_out, not_1_out);
  T_Flip_Flop t_ff_2 (.T(1'b1), .clk(t_ff_1_qn), .Q(t_ff_2_q));  // open: Qn, reset, preset
  not not_3 (not_3_out, t_ff_2_q);
  not not_4 (not_4_out, t_ff_1_q);
  and and_2 (Load, t_ff_1_q, not_3_out);
  and and_3 (Exe, not_4_out, t_ff_2_q);
  and and_4 (Sav, t_ff_1_q, t_ff_2_q);
endmodule

module OP_ROM (
  input  [7:0] IRin,
  output ADD,
  output SUB,
  output MULT,
  output LD,
  output SAV,
  output BEQ,
  output BNQ,
  output PRT,
  output INP,
  output STOP,
  output FLSH
);

  wire not_1_out, not_2_out, not_3_out, not_4_out, not_5_out, not_6_out, not_7_out, not_8_out, not_9_out,
       not_10_out, not_11_out, not_12_out, not_13_out, not_14_out, not_15_out, not_16_out, not_17_out,
       not_18_out, not_19_out, not_20_out, not_21_out, not_22_out, not_23_out, not_24_out, not_25_out,
       not_26_out, not_27_out, not_28_out, not_29_out, not_30_out, not_31_out, or_1_out;

  not not_1 (not_1_out, IRin[3]);
  not not_2 (not_2_out, IRin[4]);
  not not_3 (not_3_out, IRin[5]);
  not not_4 (not_4_out, IRin[4]);
  not not_5 (not_5_out, IRin[5]);
  not not_6 (not_6_out, IRin[5]);
  not not_7 (not_7_out, IRin[6]);
  not not_8 (not_8_out, IRin[6]);
  or or_1 (or_1_out, IRin[4], IRin[5]);
  not not_9 (not_9_out, IRin[6]);
  not not_10 (not_10_out, IRin[7]);
  not not_11 (not_11_out, IRin[7]);
  not not_12 (not_12_out, IRin[2]);
  not not_13 (not_13_out, IRin[3]);
  not not_14 (not_14_out, IRin[5]);
  not not_15 (not_15_out, IRin[3]);
  not not_16 (not_16_out, IRin[5]);
  not not_17 (not_17_out, IRin[1]);
  not not_18 (not_18_out, IRin[2]);
  not not_19 (not_19_out, IRin[3]);
  not not_20 (not_20_out, IRin[4]);
  not not_21 (not_21_out, IRin[5]);
  not not_22 (not_22_out, IRin[6]);
  not not_23 (not_23_out, IRin[7]);
  not not_24 (not_24_out, IRin[0]);
  not not_25 (not_25_out, IRin[1]);
  not not_26 (not_26_out, IRin[2]);
  not not_27 (not_27_out, IRin[3]);
  not not_28 (not_28_out, IRin[4]);
  not not_29 (not_29_out, IRin[5]);
  not not_30 (not_30_out, IRin[6]);
  not not_31 (not_31_out, IRin[7]);
  and and_1 (ADD, not_1_out, not_2_out, not_3_out, IRin[6], IRin[7]);
  and and_2 (SUB, IRin[3], not_4_out, not_5_out, IRin[6], IRin[7]);
  and and_3 (MULT, IRin[5], IRin[6], IRin[7]);
  and and_4 (LD, not_6_out, not_7_out, IRin[7]);
  and and_5 (SAV, IRin[5], not_8_out, IRin[7]);
  and and_6 (BEQ, or_1_out, not_9_out, not_10_out);
  and and_7 (BNQ, IRin[6], not_11_out);
  and and_8 (PRT, not_12_out, not_13_out, IRin[4], not_14_out, IRin[6], IRin[7]);
  and and_9 (INP, IRin[2], not_15_out, IRin[4], not_16_out, IRin[6], IRin[7]);
  and and_10 (STOP, IRin[0], not_17_out, not_18_out, not_19_out, not_20_out, not_21_out, not_22_out, not_23_out);
  and and_11 (FLSH, not_24_out, not_25_out, not_26_out, not_27_out, not_28_out, not_29_out, not_30_out, not_31_out);
endmodule

module CU (
  input  [7:0] IRin,
  input  in_2,
  output Reg0,
  output Reg1,
  output ALU_L,
  output ALU_R,
  output ALU_O,
  output STAT,
  output IR,
  output PC,
  output MAR,
  output MBR,
  output ALU_EXE,
  output R_W,
  output ALU_FLAG
);

  wire add_sub_1_done, cntr_1_exe, cntr_1_load, cntr_1_sav, op_rom_1_add, op_rom_1_sub, or_1_out, or_2_out;

  OP_ROM op_rom_1 (
    .IRin(IRin), .ADD(op_rom_1_add), .SUB(op_rom_1_sub));  // open: PRT, LD, MULT, BNQ, SAV, BEQ, INP, STOP, FLSH
  Clock clock_1 ();  // open: out
  or or_1 (or_1_out, add_sub_1_done, in_2);
  CNTR cntr_1 (.Exe(cntr_1_exe), .in_1(or_1_out), .Load(cntr_1_load), .Sav(cntr_1_sav));  // open: Fetch
  or or_2 (or_2_out, op_rom_1_add, op_rom_1_sub);
  ADD_SUB add_sub_1 (
    .IRin(IRin), .Actv(or_2_out), .LOAD(cntr_1_load), .EXE(cntr_1_exe), .SAV(cntr_1_sav),
    .DONE(add_sub_1_done), .R0(Reg0), .R1(Reg1), .R_W(R_W), .ALU_L(ALU_L), .ALU_R(ALU_R), .ALU_EXEC(ALU_EXE),
    .ALU_O(ALU_O));

  // Notes on the sheet:
  //   Control Gates
endmodule

module ADD_SUB (
  input  [7:0] IRin,
  input  Actv,
  input  LOAD,
  input  EXE,
  input  SAV,
  output DONE,
  output R0,
  output R1,
  output R_W,
  output ALU_L,
  output ALU_R,
  output ALU_EXEC,
  output ALU_O
);

  wire and_1_out, and_2_out, and_3_out, and_4_out, and_5_out, and_6_out, and_7_out, and_8_out, clock_1_out,
       clock_2_out, clock_3_out, not_1_out, not_2_out, not_3_out, or_1_out, or_2_out, or_3_out, or_4_out,
       or_6_out, or_7_out, or_8_out, t_ff_1_qn;

  or or_1 (or_1_out, ALU_R, and_1_out);
  and and_1 (and_1_out, LOAD, Actv);
  and and_2 (and_2_out, EXE, Actv);
  and and_3 (and_3_out, SAV, Actv);
  or or_2 (or_2_out, ALU_L, ALU_R);
  T_Flip_Flop t_ff_1 (.T(or_1_out), .clk(clock_1_out), .Q(ALU_L), .Qn(t_ff_1_qn), .reset(and_6_out));  // open: preset
  Clock clock_1 (.out(clock_1_out));
  T_Flip_Flop t_ff_2 (.T(or_3_out), .clk(clock_2_out), .Q(ALU_EXEC));  // open: Qn, reset, preset
  or or_3 (or_3_out, ALU_EXEC, and_2_out);
  Clock clock_2 (.out(clock_2_out));
  not not_1 (not_1_out, clock_2_out);
  T_Flip_Flop t_ff_3 (.T(or_4_out), .clk(clock_3_out), .Q(ALU_O));  // open: Qn, reset, preset
  or or_4 (or_4_out, ALU_O, and_3_out);
  Clock clock_3 (.out(clock_3_out));
  not not_2 (not_2_out, clock_3_out);
  and and_4 (and_4_out, IRin[2], ALU_L);
  and and_5 (and_5_out, IRin[1], ALU_R);
  T_Flip_Flop t_ff_4 (.T(or_1_out), .clk(t_ff_1_qn), .Q(ALU_R), .reset(and_6_out));  // open: Qn, preset
  and and_6 (and_6_out, ALU_R, ALU_L);
  and and_7 (and_7_out, ALU_EXEC, not_1_out);
  and and_8 (and_8_out, ALU_O, not_2_out);
  or or_5 (DONE, and_6_out, or_6_out);
  or or_6 (or_6_out, and_7_out, and_8_out);
  Demultiplexer #(.enable("false")) demultiplexer_1 (.out0(R0), .out1(R1), .in(or_2_out), .sel(or_7_out));
  or or_7 (or_7_out, and_4_out, and_5_out);
  not not_3 (not_3_out, and_1_out);
  or or_8 (or_8_out, not_3_out, ALU_O);
  and and_9 (R_W, or_8_out, Actv);
endmodule
