// Logisim project RAMfinalver45.circ as structural Verilog: 7 circuits, main circuit main
module main (
  input  in_1,
  input  [3:0] in_2,
  input  [7:0] in_3,
  output [7:0] out_4
);

  wire clock_1_out, mode_reg_1_output;
  wire [7:0] addr_reg_1_address_output, ram_16bytes_1_out_4, undriven;

  Clock clock_1 (.out(clock_1_out));
  RAM_16bytes ram_16bytes_1 (
    .mode_input(mode_reg_1_output), .in_3(undriven), .in_1(addr_reg_1_address_output),
    .out_4(ram_16bytes_1_out_4));
  MODE_REG mode_reg_1 (.\output (mode_reg_1_output), .\input (in_1), .in_2(clock_1_out));
  ADDR_REG addr_reg_1 (.addr_input(in_2), .address_output(addr_reg_1_address_output), .in_2(clock_1_out));
  DATA_REG data_reg_1 (
    .data_output(out_4), .out_4(ram_16bytes_1_out_4), .mode_input(clock_1_out), .in_2(undriven),
    .data_input(in_3));
endmodule

module mem_cell (
  input  \input ,
  input  mode,
  input  select,
  output \output 
);

  wire and_1_out, and_2_out, clock_1_out, not_1_out, not_2_out, s_r_ff_1_q;

  and and_1 (and_1_out, mode, select, not_1_out);
  not not_1 (not_1_out, \input );
  S_R_Flip_Flop s_r_ff_1 (.S(and_2_out), .R(and_1_out), .clk(clock_1_out), .Q(s_r_ff_1_q));  // open: reset, Qn, preset
  and and_2 (and_2_out, \input , mode, select);
  Clock clock_1 (.out(clock_1_out));
  not not_2 (not_2_out, mode);
  and and_3 (\output , s_r_ff_1_q, not_2_out, select);

  // Notes on the sheet:
  //   clk
endmodule

module RAM_16bytes (
  input  [7:0] in_1,
  input  mode_input,
  input  [7:0] in_3,
  output [7:0] out_4
);

  wire A0000_out, A0001_out, A0010_out, A0011_out, A0100_out, A0101_out, A0110_out, A0111_out, A111_out,
       A1000_out, A1001_out, A1010_out, A1011_out, A1100_out, A1101_out, A1110_out, clock_1_out, clock_2_out,
       clock_3_out, clock_4_out, clock_5_out, clock_6_out, clock_7_out, clock_8_out, clock_9_out,
       clock_10_out, clock_11_out, clock_12_out, clock_13_out, clock_14_out, clock_15_out, clock_16_out,
       mem_cell_1_output, mem_cell_2_output, mem_cell_3_output, mem_cell_4_output, mem_cell_5_output,
       mem_cell_6_output, mem_cell_7_output, mem_cell_8_output, mem_cell_9_output, mem_cell_10_output,
       mem_cell_11_output, mem_cell_12_output, mem_cell_13_output, mem_cell_14_output, mem_cell_15_output,
       mem_cell_16_output, mem_cell_17_output, mem_cell_18_output, mem_cell_19_output, mem_cell_20_output,
       mem_cell_21_output, mem_cell_22_output, mem_cell_23_output, mem_cell_24_output, mem_cell_25_output,
       mem_cell_26_output, mem_cell_27_output, mem_cell_28_output, mem_cell_29_output, mem_cell_30_output,
       mem_cell_31_output, mem_cell_32_output, mem_cell_33_output, mem_cell_34_output, mem_cell_35_output,
       mem_cell_36_output, mem_cell_37_output, mem_cell_38_output, mem_cell_39_output, mem_cell_40_output,
       mem_cell_41_output, mem_cell_42_output, mem_cell_43_output, mem_cell_44_output, mem_cell_45_output,
       mem_cell_46_output, mem_cell_47_output, mem_cell_48_output, mem_cell_49_output, mem_cell_50_output,
       mem_cell_51_output, mem_cell_52_output, mem_cell_53_output, mem_cell_54_output, mem_cell_55_output,
       mem_cell_56_output, mem_cell_57_output, mem_cell_58_output, mem_cell_59_output, mem_cell_60_output,
       mem_cell_61_output, mem_cell_62_output, mem_cell_63_output, mem_cell_64_output, mem_cell_65_output,
       mem_cell_66_output, mem_cell_67_output, mem_cell_68_output, mem_cell_69_output, mem_cell_70_output,
       mem_cell_71_output, mem_cell_72_output, mem_cell_73_output, mem_cell_74_output, mem_cell_75_output,
       mem_cell_76_output, mem_cell_77_output, mem_cell_78_output, mem_cell_79_output, mem_cell_80_output,
       mem_cell_81_output, mem_cell_82_output, mem_cell_83_output, mem_cell_84_output, mem_cell_85_output,
       mem_cell_86_output, mem_cell_87_output, mem_cell_88_output, mem_cell_89_output, mem_cell_90_output,
       mem_cell_91_output, mem_cell_92_output, mem_cell_93_output, mem_cell_94_output, mem_cell_95_output,
       mem_cell_96_output, mem_cell_97_output, mem_cell_98_output, mem_cell_99_output, mem_cell_100_output,
       mem_cell_101_output, mem_cell_102_output, mem_cell_103_output, mem_cell_104_output,
       mem_cell_105_output, mem_cell_106_output, mem_cell_107_output, mem_cell_108_output,
       mem_cell_109_output, mem_cell_110_output, mem_cell_111_output, mem_cell_112_output,
       mem_cell_113_output, mem_cell_114_output, mem_cell_115_output, mem_cell_116_output,
       mem_cell_117_output, mem_cell_118_output, mem_cell_119_output, mem_cell_120_output,
       mem_cell_121_output, mem_cell_122_output, mem_cell_123_output, mem_cell_124_output,
       mem_cell_125_output, mem_cell_126_output, mem_cell_127_output, mem_cell_128_output, not_1_out,
       not_2_out, not_3_out, not_4_out, not_5_out, not_6_out, not_7_out, not_8_out, or_1_out, or_2_out,
       or_3_out, or_4_out, or_5_out, or_6_out, or_7_out, or_8_out, or_9_out, or_10_out, or_11_out, or_12_out,
       or_13_out, or_14_out, or_15_out, or_16_out, or_17_out, or_18_out, or_19_out, or_20_out, or_21_out,
       or_22_out, or_23_out, or_24_out, or_25_out, or_26_out, or_27_out, or_28_out, or_29_out, or_30_out,
       or_31_out, or_32_out;

  and A0000 (A0000_out, in_1[7], in_1[5], in_1[3], in_1[1]);
  Clock clock_1 (.out(clock_1_out));
  mem_cell mem_cell_1 (.\input (in_3[0]), .mode(mode_input), .select(A0000_out), .\output (mem_cell_1_output));
  mem_cell mem_cell_2 (.\input (in_3[1]), .mode(mode_input), .select(A0000_out), .\output (mem_cell_2_output));
  mem_cell mem_cell_3 (.\input (in_3[2]), .mode(mode_input), .select(A0000_out), .\output (mem_cell_3_output));
  mem_cell mem_cell_4 (.\input (in_3[3]), .mode(mode_input), .select(A0000_out), .\output (mem_cell_4_output));
  mem_cell mem_cell_5 (.\input (in_3[4]), .mode(mode_input), .select(A0000_out), .\output (mem_cell_5_output));
  mem_cell mem_cell_6 (.\input (in_3[5]), .mode(mode_input), .select(A0000_out), .\output (mem_cell_6_output));
  mem_cell mem_cell_7 (.\input (in_3[6]), .mode(mode_input), .select(A0000_out), .\output (mem_cell_7_output));
  mem_cell mem_cell_8 (.\input (in_3[7]), .mode(mode_input), .select(A0000_out), .\output (mem_cell_8_output));
  and A0001 (A0001_out, in_1[7], in_1[5], in_1[3], in_1[0]);
  Clock clock_2 (.out(clock_2_out));
  mem_cell mem_cell_9 (.\input (in_3[0]), .mode(mode_input), .select(A0001_out), .\output (mem_cell_9_output));
  mem_cell mem_cell_10 (.\input (in_3[1]), .mode(mode_input), .select(A0001_out), .\output (mem_cell_10_output));
  mem_cell mem_cell_11 (.\input (in_3[2]), .mode(mode_input), .select(A0001_out), .\output (mem_cell_11_output));
  mem_cell mem_cell_12 (.\input (in_3[3]), .mode(mode_input), .select(A0001_out), .\output (mem_cell_12_output));
  mem_cell mem_cell_13 (.\input (in_3[4]), .mode(mode_input), .select(A0001_out), .\output (mem_cell_13_output));
  mem_cell mem_cell_14 (.\input (in_3[5]), .mode(mode_input), .select(A0001_out), .\output (mem_cell_14_output));
  mem_cell mem_cell_15 (.\input (in_3[6]), .mode(mode_input), .select(A0001_out), .\output (mem_cell_15_output));
  mem_cell mem_cell_16 (.\input (in_3[7]), .mode(mode_input), .select(A0001_out), .\output (mem_cell_16_output));
  and A0010 (A0010_out, in_1[7], in_1[5], in_1[2], in_1[1]);
  Clock clock_3 (.out(clock_3_out));
  mem_cell mem_cell_17 (.\input (in_3[0]), .mode(mode_input), .select(A0010_out), .\output (mem_cell_17_output));
  mem_cell mem_cell_18 (.\input (in_3[1]), .mode(mode_input), .select(A0010_out), .\output (mem_cell_18_output));
  mem_cell mem_cell_19 (.\input (in_3[2]), .mode(mode_input), .select(A0010_out), .\output (mem_cell_19_output));
  mem_cell mem_cell_20 (.\input (in_3[3]), .mode(mode_input), .select(A0010_out), .\output (mem_cell_20_output));
  mem_cell mem_cell_21 (.\input (in_3[4]), .mode(mode_input), .select(A0010_out), .\output (mem_cell_21_output));
  mem_cell mem_cell_22 (.\input (in_3[5]), .mode(mode_input), .select(A0010_out), .\output (mem_cell_22_output));
  mem_cell mem_cell_23 (.\input (in_3[6]), .mode(mode_input), .select(A0010_out), .\output (mem_cell_23_output));
  mem_cell mem_cell_24 (.\input (in_3[7]), .mode(mode_input), .select(A0010_out), .\output (mem_cell_24_output));
  and and_1 (out_4[0], or_25_out, not_1_out);
  not not_1 (not_1_out, mode_input);
  and and_2 (out_4[1], or_26_out, not_2_out);
  not not_2 (not_2_out, mode_input);
  and and_3 (out_4[2], or_27_out, not_3_out);
  not not_3 (not_3_out, mode_input);
  and and_4 (out_4[3], or_28_out, not_4_out);
  not not_4 (not_4_out, mode_input);
  and and_5 (out_4[4], or_29_out, not_5_out);
  not not_5 (not_5_out, mode_input);
  and and_6 (out_4[5], or_30_out, not_6_out);
  not not_6 (not_6_out, mode_input);
  and and_7 (out_4[6], or_31_out, not_7_out);
  not not_7 (not_7_out, mode_input);
  and and_8 (out_4[7], or_32_out, not_8_out);
  not not_8 (not_8_out, mode_input);
  and A0011 (A0011_out, in_1[7], in_1[5], in_1[2], in_1[0]);
  Clock clock_4 (.out(clock_4_out));
  mem_cell mem_cell_25 (.\input (in_3[0]), .mode(mode_input), .select(A0011_out), .\output (mem_cell_25_output));
  mem_cell mem_cell_26 (.\input (in_3[1]), .mode(mode_input), .select(A0011_out), .\output (mem_cell_26_output));
  mem_cell mem_cell_27 (.\input (in_3[2]), .mode(mode_input), .select(A0011_out), .\output (mem_cell_27_output));
  mem_cell mem_cell_28 (.\input (in_3[3]), .mode(mode_input), .select(A0011_out), .\output (mem_cell_28_output));
  mem_cell mem_cell_29 (.\input (in_3[4]), .mode(mode_input), .select(A0011_out), .\output (mem_cell_29_output));
  mem_cell mem_cell_30 (.\input (in_3[5]), .mode(mode_input), .select(A0011_out), .\output (mem_cell_30_output));
  mem_cell mem_cell_31 (.\input (in_3[6]), .mode(mode_input), .select(A0011_out), .\output (mem_cell_31_output));
  mem_cell mem_cell_32 (.\input (in_3[7]), .mode(mode_input), .select(A0011_out), .\output (mem_cell_32_output));
  and A0100 (A0100_out, in_1[7], in_1[4], in_1[3], in_1[1]);
  or or_1 (or_1_out, mem_cell_1_output, mem_cell_9_output, mem_cell_17_output, mem_cell_25_output);
  or or_2 (or_2_out, mem_cell_2_output, mem_cell_10_output, mem_cell_18_output, mem_cell_26_output);
  or or_3 (or_3_out, mem_cell_3_output, mem_cell_11_output, mem_cell_19_output, mem_cell_27_output);
  or or_4 (or_4_out, mem_cell_4_output, mem_cell_12_output, mem_cell_20_output, mem_cell_28_output);
  or or_5 (or_5_out, mem_cell_5_output, mem_cell_13_output, mem_cell_21_output, mem_cell_29_output);
  or or_6 (or_6_out, mem_cell_6_output, mem_cell_14_output, mem_cell_22_output, mem_cell_30_output);
  or or_7 (or_7_out, mem_cell_7_output, mem_cell_15_output, mem_cell_23_output, mem_cell_31_output);
  or or_8 (or_8_out, mem_cell_8_output, mem_cell_16_output, mem_cell_24_output, mem_cell_32_output);
  Clock clock_5 (.out(clock_5_out));
  mem_cell mem_cell_33 (.\input (in_3[0]), .mode(mode_input), .select(A0100_out), .\output (mem_cell_33_output));
  mem_cell mem_cell_34 (.\input (in_3[1]), .mode(mode_input), .select(A0100_out), .\output (mem_cell_34_output));
  mem_cell mem_cell_35 (.\input (in_3[2]), .mode(mode_input), .select(A0100_out), .\output (mem_cell_35_output));
  mem_cell mem_cell_36 (.\input (in_3[3]), .mode(mode_input), .select(A0100_out), .\output (mem_cell_36_output));
  mem_cell mem_cell_37 (.\input (in_3[4]), .mode(mode_input), .select(A0100_out), .\output (mem_cell_37_output));
  mem_cell mem_cell_38 (.\input (in_3[5]), .mode(mode_input), .select(A0100_out), .\output (mem_cell_38_output));
  mem_cell mem_cell_39 (.\input (in_3[6]), .mode(mode_input), .select(A0100_out), .\output (mem_cell_39_output));
  mem_cell mem_cell_40 (.\input (in_3[7]), .mode(mode_input), .select(A0100_out), .\output (mem_cell_40_output));
  and A0101 (A0101_out, in_1[7], in_1[4], in_1[3], in_1[0]);
  Clock clock_6 (.out(clock_6_out));
  mem_cell mem_cell_41 (.\input (in_3[0]), .mode(mode_input), .select(A0101_out), .\output (mem_cell_41_output));
  mem_cell mem_cell_42 (.\input (in_3[1]), .mode(mode_input), .select(A0101_out), .\output (mem_cell_42_output));
  mem_cell mem_cell_43 (.\input (in_3[2]), .mode(mode_input), .select(A0101_out), .\output (mem_cell_43_output));
  mem_cell mem_cell_44 (.\input (in_3[3]), .mode(mode_input), .select(A0101_out), .\output (mem_cell_44_output));
  mem_cell mem_cell_45 (.\input (in_3[4]), .mode(mode_input), .select(A0101_out), .\output (mem_cell_45_output));
  mem_cell mem_cell_46 (.\input (in_3[5]), .mode(mode_input), .select(A0101_out), .\output (mem_cell_46_output));
  mem_cell mem_cell_47 (.\input (in_3[6]), .mode(mode_input), .select(A0101_out), .\output (mem_cell_47_output));
  mem_cell mem_cell_48 (.\input (in_3[7]), .mode(mode_input), .select(A0101_out), .\output (mem_cell_48_output));
  and A0110 (A0110_out, in_1[7], in_1[4], in_1[2], in_1[1]);
  Clock clock_7 (.out(clock_7_out));
  mem_cell mem_cell_49 (.\input (in_3[0]), .mode(mode_input), .select(A0110_out), .\output (mem_cell_49_output));
  mem_cell mem_cell_50 (.\input (in_3[1]), .mode(mode_input), .select(A0110_out), .\output (mem_cell_50_output));
  mem_cell mem_cell_51 (.\input (in_3[2]), .mode(mode_input), .select(A0110_out), .\output (mem_cell_51_output));
  mem_cell mem_cell_52 (.\input (in_3[3]), .mode(mode_input), .select(A0110_out), .\output (mem_cell_52_output));
  mem_cell mem_cell_53 (.\input (in_3[4]), .mode(mode_input), .select(A0110_out), .\output (mem_cell_53_output));
  mem_cell mem_cell_54 (.\input (in_3[5]), .mode(mode_input), .select(A0110_out), .\output (mem_cell_54_output));
  mem_cell mem_cell_55 (.\input (in_3[6]), .mode(mode_input), .select(A0110_out), .\output (mem_cell_55_output));
  mem_cell mem_cell_56 (.\input (in_3[7]), .mode(mode_input), .select(A0110_out), .\output (mem_cell_56_output));
  and A0111 (A0111_out, in_1[7], in_1[4], in_1[2], in_1[0]);
  Clock clock_8 (.out(clock_8_out));
  mem_cell mem_cell_57 (.\input (in_3[0]), .mode(mode_input), .select(A0111_out), .\output (mem_cell_57_output));
  mem_cell mem_cell_58 (.\input (in_3[1]), .mode(mode_input), .select(A0111_out), .\output (mem_cell_58_output));
  mem_cell mem_cell_59 (.\input (in_3[2]), .mode(mode_input), .select(A0111_out), .\output (mem_cell_59_output));
  mem_cell mem_cell_60 (.\input (in_3[3]), .mode(mode_input), .select(A0111_out), .\output (mem_cell_60_output));
  mem_cell mem_cell_61 (.\input (in_3[4]), .mode(mode_input), .select(A0111_out), .\output (mem_cell_61_output));
  mem_cell mem_cell_62 (.\input (in_3[5]), .mode(mode_input), .select(A0111_out), .\output (mem_cell_62_output));
  mem_cell mem_cell_63 (.\input (in_3[6]), .mode(mode_input), .select(A0111_out), .\output (mem_cell_63_output));
  mem_cell mem_cell_64 (.\input (in_3[7]), .mode(mode_input), .select(A0111_out), .\output (mem_cell_64_output));
  or or_9 (or_9_out, mem_cell_33_output, mem_cell_41_output, or_1_out, mem_cell_49_output, mem_cell_57_output);
  or or_10 (or_10_out, mem_cell_34_output, mem_cell_42_output, or_2_out, mem_cell_50_output, mem_cell_58_output);
  or or_11 (or_11_out, mem_cell_35_output, mem_cell_43_output, or_3_out, mem_cell_51_output, mem_cell_59_output);
  or or_12 (or_12_out, mem_cell_36_output, mem_cell_44_output, or_4_out, mem_cell_52_output, mem_cell_60_output);
  or or_13 (or_13_out, mem_cell_37_output, mem_cell_45_output, or_5_out, mem_cell_53_output, mem_cell_61_output);
  or or_14 (or_14_out, mem_cell_38_output, mem_cell_46_output, or_6_out, mem_cell_54_output, mem_cell_62_output);
  or or_15 (or_15_out, mem_cell_39_output, mem_cell_47_output, or_7_out, mem_cell_55_output, mem_cell_63_output);
  or or_16 (or_16_out, mem_cell_40_output, mem_cell_48_output, or_8_out, mem_cell_56_output, mem_cell_64_output);
  and A1000 (A1000_out, in_1[6], in_1[5], in_1[3], in_1[1]);
  Clock clock_9 (.out(clock_9_out));
  mem_cell mem_cell_65 (.\input (in_3[0]), .mode(mode_input), .select(A1000_out), .\output (mem_cell_65_output));
  mem_cell mem_cell_66 (.\input (in_3[1]), .mode(mode_input), .select(A1000_out), .\output (mem_cell_66_output));
  mem_cell mem_cell_67 (.\input (in_3[2]), .mode(mode_input), .select(A1000_out), .\output (mem_cell_67_output));
  mem_cell mem_cell_68 (.\input (in_3[3]), .mode(mode_input), .select(A1000_out), .\output (mem_cell_68_output));
  mem_cell mem_cell_69 (.\input (in_3[4]), .mode(mode_input), .select(A1000_out), .\output (mem_cell_69_output));
  mem_cell mem_cell_70 (.\input (in_3[5]), .mode(mode_input), .select(A1000_out), .\output (mem_cell_70_output));
  mem_cell mem_cell_71 (.\input (in_3[6]), .mode(mode_input), .select(A1000_out), .\output (mem_cell_71_output));
  mem_cell mem_cell_72 (.\input (in_3[7]), .mode(mode_input), .select(A1000_out), .\output (mem_cell_72_output));
  and A1001 (A1001_out, in_1[6], in_1[5], in_1[3], in_1[0]);
  Clock clock_10 (.out(clock_10_out));
  mem_cell mem_cell_73 (.\input (in_3[0]), .mode(mode_input), .select(A1001_out), .\output (mem_cell_73_output));
  mem_cell mem_cell_74 (.\input (in_3[1]), .mode(mode_input), .select(A1001_out), .\output (mem_cell_74_output));
  mem_cell mem_cell_75 (.\input (in_3[2]), .mode(mode_input), .select(A1001_out), .\output (mem_cell_75_output));
  mem_cell mem_cell_76 (.\input (in_3[3]), .mode(mode_input), .select(A1001_out), .\output (mem_cell_76_output));
  mem_cell mem_cell_77 (.\input (in_3[4]), .mode(mode_input), .select(A1001_out), .\output (mem_cell_77_output));
  mem_cell mem_cell_78 (.\input (in_3[5]), .mode(mode_input), .select(A1001_out), .\output (mem_cell_78_output));
  mem_cell mem_cell_79 (.\input (in_3[6]), .mode(mode_input), .select(A1001_out), .\output (mem_cell_79_output));
  mem_cell mem_cell_80 (.\input (in_3[7]), .mode(mode_input), .select(A1001_out), .\output (mem_cell_80_output));
  and A1010 (A1010_out, in_1[6], in_1[5], in_1[2], in_1[1]);
  Clock clock_11 (.out(clock_11_out));
  mem_cell mem_cell_81 (.\input (in_3[0]), .mode(mode_input), .select(A1010_out), .\output (mem_cell_81_output));
  mem_cell mem_cell_82 (.\input (in_3[1]), .mode(mode_input), .select(A1010_out), .\output (mem_cell_82_output));
  mem_cell mem_cell_83 (.\input (in_3[2]), .mode(mode_input), .select(A1010_out), .\output (mem_cell_83_output));
  mem_cell mem_cell_84 (.\input (in_3[3]), .mode(mode_input), .select(A1010_out), .\output (mem_cell_84_output));
  mem_cell mem_cell_85 (.\input (in_3[4]), .mode(mode_input), .select(A1010_out), .\output (mem_cell_85_output));
  mem_cell mem_cell_86 (.\input (in_3[5]), .mode(mode_input), .select(A1010_out), .\output (mem_cell_86_output));
  mem_cell mem_cell_87 (.\input (in_3[6]), .mode(mode_input), .select(A1010_out), .\output (mem_cell_87_output));
  mem_cell mem_cell_88 (.\input (in_3[7]), .mode(mode_input), .select(A1010_out), .\output (mem_cell_88_output));
  and A1011 (A1011_out, in_1[6], in_1[5], in_1[2], in_1[0]);
  Clock clock_12 (.out(clock_12_out));
  mem_cell mem_cell_89 (.\input (in_3[0]), .mode(mode_input), .select(A1011_out), .\output (mem_cell_89_output));
  mem_cell mem_cell_90 (.\input (in_3[1]), .mode(mode_input), .select(A1011_out), .\output (mem_cell_90_output));
  mem_cell mem_cell_91 (.\input (in_3[2]), .mode(mode_input), .select(A1011_out), .\output (mem_cell_91_output));
  mem_cell mem_cell_92 (.\input (in_3[3]), .mode(mode_input), .select(A1011_out), .\output (mem_cell_92_output));
  mem_cell mem_cell_93 (.\input (in_3[4]), .mode(mode_input), .select(A1011_out), .\output (mem_cell_93_output));
  mem_cell mem_cell_94 (.\input (in_3[5]), .mode(mode_input), .select(A1011_out), .\output (mem_cell_94_output));
  mem_cell mem_cell_95 (.\input (in_3[6]), .mode(mode_input), .select(A1011_out), .\output (mem_cell_95_output));
  mem_cell mem_cell_96 (.\input (in_3[7]), .mode(mode_input), .select(A1011_out), .\output (mem_cell_96_output));
  and A1100 (A1100_out, in_1[6], in_1[4], in_1[3], in_1[1]);
  or or_17 (or_17_out, mem_cell_65_output, mem_cell_73_output, or_9_out, mem_cell_81_output, mem_cell_89_output);
  or or_18 (or_18_out, mem_cell_66_output, mem_cell_74_output, or_10_out, mem_cell_82_output, mem_cell_90_output);
  or or_19 (or_19_out, mem_cell_67_output, mem_cell_75_output, or_11_out, mem_cell_83_output, mem_cell_91_output);
  or or_20 (or_20_out, mem_cell_68_output, mem_cell_76_output, or_12_out, mem_cell_84_output, mem_cell_92_output);
  or or_21 (or_21_out, mem_cell_69_output, mem_cell_77_output, or_13_out, mem_cell_85_output, mem_cell_93_output);
  or or_22 (or_22_out, mem_cell_70_output, mem_cell_78_output, or_14_out, mem_cell_86_output, mem_cell_94_output);
  or or_23 (or_23_out, mem_cell_71_output, mem_cell_79_output, or_15_out, mem_cell_87_output, mem_cell_95_output);
  or or_24 (or_24_out, mem_cell_72_output, mem_cell_80_output, or_16_out, mem_cell_88_output, mem_cell_96_output);
  Clock clock_13 (.out(clock_13_out));
  mem_cell mem_cell_97 (.\input (in_3[0]), .mode(mode_input), .select(A1100_out), .\output (mem_cell_97_output));
  mem_cell mem_cell_98 (.\input (in_3[1]), .mode(mode_input), .select(A1100_out), .\output (mem_cell_98_output));
  mem_cell mem_cell_99 (.\input (in_3[2]), .mode(mode_input), .select(A1100_out), .\output (mem_cell_99_output));
  mem_cell mem_cell_100 (.\input (in_3[3]), .mode(mode_input), .select(A1100_out), .\output (mem_cell_100_output));
  mem_cell mem_cell_101 (.\input (in_3[4]), .mode(mode_input), .select(A1100_out), .\output (mem_cell_101_output));
  mem_cell mem_cell_102 (.\input (in_3[5]), .mode(mode_input), .select(A1100_out), .\output (mem_cell_102_output));
  mem_cell mem_cell_103 (.\input (in_3[6]), .mode(mode_input), .select(A1100_out), .\output (mem_cell_103_output));
  mem_cell mem_cell_104 (.\input (in_3[7]), .mode(mode_input), .select(A1100_out), .\output (mem_cell_104_output));
  and A1101 (A1101_out, in_1[6], in_1[4], in_1[3], in_1[0]);
  Clock clock_14 (.out(clock_14_out));
  mem_cell mem_cell_105 (.\input (in_3[0]), .mode(mode_input), .select(A1101_out), .\output (mem_cell_105_output));
  mem_cell mem_cell_106 (.\input (in_3[1]), .mode(mode_input), .select(A1101_out), .\output (mem_cell_106_output));
  mem_cell mem_cell_107 (.\input (in_3[2]), .mode(mode_input), .select(A1101_out), .\output (mem_cell_107_output));
  mem_cell mem_cell_108 (.\input (in_3[3]), .mode(mode_input), .select(A1101_out), .\output (mem_cell_108_output));
  mem_cell mem_cell_109 (.\input (in_3[4]), .mode(mode_input), .select(A1101_out), .\output (mem_cell_109_output));
  mem_cell mem_cell_110 (.\input (in_3[5]), .mode(mode_input), .select(A1101_out), .\output (mem_cell_110_output));
  mem_cell mem_cell_111 (.\input (in_3[6]), .mode(mode_input), .select(A1101_out), .\output (mem_cell_111_output));
  mem_cell mem_cell_112 (.\input (in_3[7]), .mode(mode_input), .select(A1101_out), .\output (mem_cell_112_output));
  and A1110 (A1110_out, in_1[6], in_1[4], in_1[2], in_1[1]);
  Clock clock_15 (.out(clock_15_out));
  mem_cell mem_cell_113 (.\input (in_3[0]), .mode(mode_input), .select(A1110_out), .\output (mem_cell_113_output));
  mem_cell mem_cell_114 (.\input (in_3[1]), .mode(mode_input), .select(A1110_out), .\output (mem_cell_114_output));
  mem_cell mem_cell_115 (.\input (in_3[2]), .mode(mode_input), .select(A1110_out), .\output (mem_cell_115_output));
  mem_cell mem_cell_116 (.\input (in_3[3]), .mode(mode_input), .select(A1110_out), .\output (mem_cell_116_output));
  mem_cell mem_cell_117 (.\input (in_3[4]), .mode(mode_input), .select(A1110_out), .\output (mem_cell_117_output));
  mem_cell mem_cell_118 (.\input (in_3[5]), .mode(mode_input), .select(A1110_out), .\output (mem_cell_118_output));
  mem_cell mem_cell_119 (.\input (in_3[6]), .mode(mode_input), .select(A1110_out), .\output (mem_cell_119_output));
  mem_cell mem_cell_120 (.\input (in_3[7]), .mode(mode_input), .select(A1110_out), .\output (mem_cell_120_output));
  and A111 (A111_out, in_1[6], in_1[4], in_1[2], in_1[0]);
  Clock clock_16 (.out(clock_16_out));
  mem_cell mem_cell_121 (.\input (in_3[0]), .mode(mode_input), .select(A111_out), .\output (mem_cell_121_output));
  mem_cell mem_cell_122 (.\input (in_3[1]), .mode(mode_input), .select(A111_out), .\output (mem_cell_122_output));
  mem_cell mem_cell_123 (.\input (in_3[2]), .mode(mode_input), .select(A111_out), .\output (mem_cell_123_output));
  mem_cell mem_cell_124 (.\input (in_3[3]), .mode(mode_input), .select(A111_out), .\output (mem_cell_124_output));
  mem_cell mem_cell_125 (.\input (in_3[4]), .mode(mode_input), .select(A111_out), .\output (mem_cell_125_output));
  mem_cell mem_cell_126 (.\input (in_3[5]), .mode(mode_input), .select(A111_out), .\output (mem_cell_126_output));
  mem_cell mem_cell_127 (.\input (in_3[6]), .mode(mode_input), .select(A111_out), .\output (mem_cell_127_output));
  mem_cell mem_cell_128 (.\input (in_3[7]), .mode(mode_input), .select(A111_out), .\output (mem_cell_128_output));
  or or_25 (or_25_out, mem_cell_97_output, mem_cell_105_output, or_17_out, mem_cell_113_output, mem_cell_121_output);
  or or_26 (or_26_out, mem_cell_98_output, mem_cell_106_output, or_18_out, mem_cell_114_output, mem_cell_122_output);
  or or_27 (or_27_out, mem_cell_99_output, mem_cell_107_output, or_19_out, mem_cell_115_output, mem_cell_123_output);
  or or_28 (or_28_out, mem_cell_100_output, mem_cell_108_output, or_20_out, mem_cell_116_output, mem_cell_124_output);
  or or_29 (or_29_out, mem_cell_101_output, mem_cell_109_output, or_21_out, mem_cell_117_output, mem_cell_125_output);
  or or_30 (or_30_out, mem_cell_102_output, mem_cell_110_output, or_22_out, mem_cell_118_output, mem_cell_126_output);
  or or_31 (or_31_out, mem_cell_103_output, mem_cell_111_output, or_23_out, mem_cell_119_output, mem_cell_127_output);
  or or_32 (or_32_out, mem_cell_104_output, mem_cell_112_output, or_24_out, mem_cell_120_output, mem_cell_128_output);

  // Notes on the sheet:
  //   data input
  //   address input
  //   address space
  //   data space
  //   RAM
  //   data output
endmodule

module ADDR_REG (
  input  [3:0] addr_input,
  input  in_2,
  output [7:0] address_output
);

  D_Flip_Flop d_ff_1 (.D(addr_input[0]), .clk(in_2), .Q(address_output[0]));  // open: Qn, preset, reset
  D_Flip_Flop d_ff_2 (.D(addr_input[1]), .clk(in_2), .Q(address_output[2]));  // open: Qn, preset, reset
  D_Flip_Flop d_ff_3 (.D(addr_input[2]), .clk(in_2), .Q(address_output[4]));  // open: Qn, preset, reset
  D_Flip_Flop d_ff_4 (.D(addr_input[3]), .clk(in_2), .Q(address_output[6]));  // open: Qn, preset, reset
  not not_1 (address_output[1], address_output[0]);
  not not_2 (address_output[3], address_output[2]);
  not not_3 (address_output[5], address_output[4]);
  not not_4 (address_output[7], address_output[6]);

  // Notes on the sheet:
  //   ADDRESS REGISTER
endmodule

module DATA_REG (
  input  [7:0] data_input,
  input  [7:0] in_2,
  input  mode_input,
  output [7:0] out_4,
  output [7:0] data_output
);

  wire and_1_out, and_2_out, and_3_out, and_4_out, and_5_out, and_6_out, and_7_out, and_8_out, clock_1_out,
       clock_2_out, not_1_out, not_2_out, not_3_out, not_4_out, not_5_out, not_6_out, not_7_out, not_8_out;

  and and_1 (and_1_out, mode_input, data_input[0]);
  and and_2 (and_2_out, data_input[1], mode_input);
  and and_3 (and_3_out, mode_input, data_input[2]);
  and and_4 (and_4_out, data_input[3], mode_input);
  and and_5 (and_5_out, mode_input, data_input[4]);
  and and_6 (and_6_out, data_input[5], mode_input);
  and and_7 (and_7_out, mode_input, data_input[6]);
  and and_8 (and_8_out, data_input[7], mode_input);
  D_Flip_Flop d_ff_1 (.D(and_1_out), .clk(clock_1_out), .Q(out_4[0]));  // open: Qn, preset, reset
  Clock clock_1 (.out(clock_1_out));
  D_Flip_Flop d_ff_2 (.D(and_2_out), .clk(clock_1_out), .Q(out_4[1]));  // open: Qn, preset, reset
  D_Flip_Flop d_ff_3 (.D(and_3_out), .clk(clock_1_out), .Q(out_4[2]));  // open: Qn, preset, reset
  D_Flip_Flop d_ff_4 (.D(and_4_out), .clk(clock_1_out), .Q(out_4[3]));  // open: Qn, preset, reset
  D_Flip_Flop d_ff_5 (.D(and_5_out), .clk(clock_2_out), .Q(out_4[4]));  // open: Qn, preset, reset
  Clock clock_2 (.out(clock_2_out));
  D_Flip_Flop d_ff_6 (.D(and_6_out), .clk(clock_2_out), .Q(out_4[5]));  // open: Qn, preset, reset
  D_Flip_Flop d_ff_7 (.D(and_7_out), .clk(clock_2_out), .Q(out_4[6]));  // open: Qn, preset, reset
  D_Flip_Flop d_ff_8 (.D(and_8_out), .clk(clock_2_out), .Q(out_4[7]));  // open: Qn, preset, reset
  and and_9 (data_output[7], in_2[7], not_1_out);
  not not_1 (not_1_out, mode_input);
  and and_10 (data_output[6], in_2[6], not_2_out);
  not not_2 (not_2_out, mode_input);
  and and_11 (data_output[5], in_2[5], not_3_out);
  not not_3 (not_3_out, mode_input);
  and and_12 (data_output[4], in_2[4], not_4_out);
  not not_4 (not_4_out, mode_input);
  and and_13 (data_output[3], in_2[3], not_5_out);
  not not_5 (not_5_out, mode_input);
  and and_14 (data_output[2], in_2[2], not_6_out);
  not not_6 (not_6_out, mode_input);
  and and_15 (data_output[1], in_2[1], not_7_out);
  not not_7 (not_7_out, mode_input);
  and and_16 (data_output[0], in_2[0], not_8_out);
  not not_8 (not_8_out, mode_input);

  // Notes on the sheet:
  //   DATA REGISTER
  //   clk
  //   clk
  //   data to 16 byte RAM
  //   data from 16 byte RAM
endmodule

module MODE_REG (
  input  \input ,
  input  in_2,
  output \output 
);

  wire not_1_out;

  J_K_Flip_Flop j_k_ff_1 (.J(\input ), .K(not_1_out), .clk(in_2), .Q(\output ));  // open: Qn, preset, reset
  not not_1 (not_1_out, \input );
endmodule

module MBR (
  input  in_1,
  input  in_2,
  input  in_3,
  input  in_4,
  input  in_5,
  input  in_6,
  input  in_7,
  input  in_8,
  input  in_9,
  input  in_10,
  output out_11,
  output out_12,
  output out_13,
  output out_14,
  output out_15,
  output out_16,
  output out_17,
  output out_18
);

  wire clock_1_out;

  Clock clock_1 (.out(clock_1_out));
  mem_cell mem_cell_1 (.\input (in_2), .mode(in_1), .select(in_10), .\output (out_11));
  mem_cell mem_cell_2 (.\input (in_3), .mode(in_1), .select(in_10), .\output (out_12));
  mem_cell mem_cell_3 (.\input (in_4), .mode(in_1), .select(in_10), .\output (out_13));
  mem_cell mem_cell_4 (.\input (in_5), .mode(in_1), .select(in_10), .\output (out_14));
  mem_cell mem_cell_5 (.\input (in_6), .mode(in_1), .select(in_10), .\output (out_15));
  mem_cell mem_cell_6 (.\input (in_7), .mode(in_1), .select(in_10), .\output (out_16));
  mem_cell mem_cell_7 (.\input (in_8), .mode(in_1), .select(in_10), .\output (out_17));
  mem_cell mem_cell_8 (.\input (in_9), .mode(in_1), .select(in_10), .\output (out_18));

  // Notes on the sheet:
  //   mode
endmodule
